# Fritzing sketch FullArduinoHouse (saved by Fritzing 0.9.5d)
breadboards: 1

parts:
  Bauteil1 = Arduino Nano 33 IOT
  R1 = Resistor [tolerance=±1% resistance=1 package="2512 [SMD]"]
  R2 = Resistor [tolerance=±1% resistance=330 package="2512 [SMD]"]
  U1 = Sharp PC817 [package=THT]
  C1 = Electrolytic Capacitor [capacitance=0.1µF voltage=50V package="100 mil [THT, electrolytic]"]
  Moisture = female pin header, 2 pins [form="♀ (female)"]
  Fan = female pin header, 3 pins [form="♀ (female)"]
  Light = female pin header, 4 pins [form="♀ (female)"]
  RTC = DS1307 [package=so08]
  SHT31 = Generic female header - 5 pins [form="♀ (female)" package=THT]

nets:
  N1: Bauteil1.RESET, Bauteil1.A7
  GND: Bauteil1.GND, Bauteil1.D13~, U1.Pin_2, C1.-, Moisture.pin1, Fan.pin3, Light.pin1, RTC.GND, SHT31.GND
  N2: Bauteil1.D2, Fan.pin2
  N3: Bauteil1.D3~, Light.pin2
  N4: Bauteil1.D4, R1.Pin_0
  N5: Bauteil1.D7, SHT31.INT
  N6: Bauteil1.D11/MOSI, Bauteil1.+5V
  5V: Bauteil1.VIN, RTC.VCC, SHT31.Vcc
  N7: Bauteil1.A5, RTC.SCL, SHT31.SCL
  N8: Bauteil1.A4, RTC.SDA, SHT31.SDA
  N9: Bauteil1.A1, Fan.pin1
  N10: Bauteil1.A0, Moisture.pin2
  N11: R1.Pin_1, R2.Pin_0, C1.+
  N12: R2.Pin_1, U1.Pin_1
  N13: U1.Pin_4, Light.pin3
  N14: U1.Pin_3, Light.pin4

custom parts:
  Arduino Nano 33 IOT: The Arduino Nano 33 IoT is the easiest and cheapest point of entry to enhance existing devices (and creating new ones) to be part of the IoT and designing pico-network applications. Whether you are looking at building a sensor network connected to your office or home router, or if you want to create a BLE device sending data to a cellphone, the Nano 33 IoT is your one-stop-solution for many of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
  Generic female header - 5 pins: Generic female header
